// Logisim project MIPSProcessor_JeongYunseo_final_2success.circ as structural Verilog: 19 circuits, main circuit main
module main (
  input  [7:0] in_1,
  input  in_2,
  input  in_3,
  input  [31:0] in_4,
  output [31:0] out_5
);

  RAM #(.dataWidth(32), .databus("bibus")) ram_1 (
    .addr(in_1), .we(in_2), .clk(in_3), .din(in_4), .dout(out_5));  // open: oe

  // Notes on the sheet:
  //   write
  //   read
endmodule

module RAMtest (
  input  [7:0] in_1,
  input  in_2,
  input  in_3,
  input  [31:0] in_4,
  output [31:0] out_5
);

  RAM #(.dataWidth(32), .databus("bibus")) ram_1 (
    .addr(in_1), .we(in_2), .clk(in_3), .din(in_4), .dout(out_5));  // open: oe

  // Notes on the sheet:
  //   write
  //   read
endmodule

module ROMtest (
  input  [7:0] in_1,
  output [31:0] out_2
);

  ROM #(.dataWidth(32)) rom_1 (.addr(in_1), .data(out_2));

  // Notes on the sheet:
  //   contents of rom_1 (hex, n*v repeats v):
  //   a123fffd ffffffff 80200000
endmodule

module IF (
  input  CLK,
  input  Reset,
  input  [31:0] imm,
  input  beq,
  input  zero,
  input  bne,
  input  Not_zero,
  output [31:0] out_8
);

  wire and_1_out, and_2_out, or_1_out;
  wire [31:0] adder_1_out, adder_2_out, multiplexer_1_out, register_1_q, shifter_1_out;

  Register #(.width(32)) register_1 (.D(multiplexer_1_out), .en(1'b1), .clk(CLK), .Q(register_1_q), .clr(Reset));
  Shifter #(.width(32)) shifter_1 (.in(imm), .\dist (5'b00010), .out(shifter_1_out));
  and and_1 (and_1_out, beq, zero);
  and and_2 (and_2_out, bne, Not_zero);
  Adder #(.width(32)) adder_1 (.a(32'h4), .b(register_1_q), .out(adder_1_out));  // open: cin, cout
  or or_1 (or_1_out, and_1_out, and_2_out);
  Adder #(.width(32)) adder_2 (.a(register_1_q), .b(shifter_1_out), .out(adder_2_out));  // open: cin, cout
  Multiplexer #(.width(32), .enable("false")) multiplexer_1 (
    .in0(adder_1_out), .in1(adder_2_out), .out(multiplexer_1_out), .sel(or_1_out));
  ROM #(.dataWidth(32)) rom_1 (.addr(register_1_q[9:2]), .data(out_8));

  // Notes on the sheet:
  //   contents of rom_1 (hex, n*v repeats v):
  //   20050005 20020001 20030001 20010002 432020 601020 801820 20210001 14a1fffc
endmodule

module MIPSProcessor (
  input  Reset,
  input  CLK
);

  wire alu_1_not_zero, alu_1_zero, instruction_decode_1_memread, instruction_decode_1_memtoreg,
       instruction_decode_1_memwrite, instruction_decode_1_pcsrc;
  wire [2:0] instruction_decode_1_aluoperation;
  wire [31:0] alu_1_c, if_1_out_8, instruction_decode_1_a, instruction_decode_1_b,
       instruction_decode_1_dataforsw, instruction_decode_1_imm, multiplexer_1_out, ram_1_dout;

  IF if_1 (
    .CLK(CLK), .Reset(Reset), .imm(instruction_decode_1_imm), .beq(instruction_decode_1_pcsrc),
    .zero(alu_1_zero), .bne(instruction_decode_1_pcsrc), .Not_zero(alu_1_not_zero), .out_8(if_1_out_8));
  Multiplexer #(.width(32), .enable("false")) multiplexer_1 (
    .in0(alu_1_c), .in1(ram_1_dout), .out(multiplexer_1_out), .sel(instruction_decode_1_memtoreg));
  Instruction_Decode instruction_decode_1 (
    .instr(if_1_out_8), .CLK(CLK), .C_value_in(multiplexer_1_out), .A(instruction_decode_1_a),
    .B(instruction_decode_1_b), .dataforSW(instruction_decode_1_dataforsw), .imm(instruction_decode_1_imm),
    .ALUoperation(instruction_decode_1_aluoperation), .MemRead(instruction_decode_1_memread),
    .MemWrite(instruction_decode_1_memwrite), .MemtoReg(instruction_decode_1_memtoreg),
    .PCSrc(instruction_decode_1_pcsrc));
  ALU alu_1 (
    .A(instruction_decode_1_a), .B(instruction_decode_1_b), .Sel(instruction_decode_1_aluoperation),
    .C(alu_1_c), .zero(alu_1_zero), .Not_zero(alu_1_not_zero));
  RAM #(.dataWidth(32), .databus("bibus")) ram_1 (
    .addr(alu_1_c[9:2]), .we(instruction_decode_1_memwrite), .oe(instruction_decode_1_memread), .clk(CLK),
    .din(instruction_decode_1_dataforsw), .dout(ram_1_dout));

  // Notes on the sheet:
  //   C is input
endmodule

// ID
module Instruction_Decode (
  input  [31:0] instr,
  input  CLK,
  input  [31:0] C_value_in,
  output [31:0] A,
  output [31:0] B,
  output [31:0] dataforSW,
  output [31:0] imm,
  output [2:0] ALUoperation,
  output MemRead,
  output MemWrite,
  output MemtoReg,
  output PCSrc
);

  wire [2:0] rom_2_data;
  wire [4:0] multiplexer_1_out, rom_1_data;

  ROM #(.addrWidth(6), .dataWidth(9)) rom_1 (
    .addr(instr[31:26]), .data({PCSrc, MemtoReg, MemWrite, MemRead, rom_1_data}));
  Multiplexer #(.width(5), .enable("false")) multiplexer_1 (
    .in0(instr[15:11]), .in1(instr[20:16]), .out(multiplexer_1_out), .sel(rom_1_data[4]));
  RegisterFile32 registerfile32_1 (
    .w_data(C_value_in), .write_enable(rom_1_data[3]), .write_addr(multiplexer_1_out), .CLK(CLK),
    .A_addr(instr[25:21]), .B_addr(instr[20:16]), .A(A), .B(dataforSW));
  Multiplexer #(.width(32), .enable("false")) multiplexer_2 (.in0(dataforSW), .in1(imm), .out(B), .sel(rom_1_data[4]));
  assign imm = {{16{instr[15]}}, instr[15:0]};  // Bit_Extender bit_extender_1
  ROM #(.addrWidth(6), .dataWidth(3)) rom_2 (.addr(instr[5:0]), .data(rom_2_data));
  Multiplexer #(.width(3), .enable("false")) multiplexer_3 (
    .in0(rom_2_data), .in1(rom_1_data[2:0]), .out(ALUoperation), .sel(rom_1_data[4]));

  // Notes on the sheet:
  //   R-format:0 0 0 0 0 1 000
  //   lw: 0 /1 0 1 1 /1 000
  //   sw: 0/ 0 1 0 1/ 0 000
  //   beq: 1/ 0 0 0 0/ 0 000
  //   addi: 0/ 0 0 0 1/ 1 000
  //   bne: 1/ 0 0 0 0/ 0 000
  //   contents of rom_1 (hex, n*v repeats v):
  //   8 0 0 0 100 100 0 0 18 26*0 b8 7*0 50
  //   op lw: 10/0011
  //   op sw: 10/1011
  //   op beq: 00/0100
  //   op addi: 00/1000
  //   op bne: 00/0101
  //   R-type
  //   func
  //   shmat
  //   rd
  //   rt
  //   rs
  //   op
  //   I-type
  //   imm
  //   rt
  //   rs
  //   op
  //   강의 영상보기
  //   RegWrite
  //   ALUsrc
  //   branch/sw not update reg
  //   end
  //   start
  //   selbit=0, R-format
  //   R-type's function part->because we dont know opcode in R-format
  //   addition:000
endmodule

module RegisterFile4 (
  input  [31:0] w_data,
  input  write_enable,
  input  [1:0] write_address,
  input  clock,
  input  [1:0] A_addr,
  input  [1:0] B_addr,
  output [31:0] A,
  output [31:0] B
);

  wire demultiplexer_1_out0, demultiplexer_1_out1, demultiplexer_1_out2, demultiplexer_1_out3;
  wire [31:0] register_1_q, register_2_q, register_3_q, register_4_q;

  Demultiplexer #(.select(2), .enable("false")) demultiplexer_1 (
    .out0(demultiplexer_1_out0), .out1(demultiplexer_1_out1), .out2(demultiplexer_1_out2),
    .out3(demultiplexer_1_out3), .in(write_enable), .sel(write_address));
  Register #(.width(32)) register_1 (
    .D(w_data), .en(demultiplexer_1_out0), .clk(clock), .Q(register_1_q));  // open: clr
  Register #(.width(32)) register_2 (
    .D(w_data), .en(demultiplexer_1_out1), .clk(clock), .Q(register_2_q));  // open: clr
  Register #(.width(32)) register_3 (
    .D(w_data), .en(demultiplexer_1_out2), .clk(clock), .Q(register_3_q));  // open: clr
  Register #(.width(32)) register_4 (
    .D(w_data), .en(demultiplexer_1_out3), .clk(clock), .Q(register_4_q));  // open: clr
  Multiplexer #(.select(2), .width(32), .enable("false")) multiplexer_1 (
    .in0(register_1_q), .in1(register_2_q), .in2(register_3_q), .in3(register_4_q), .out(A), .sel(A_addr));
  Multiplexer #(.select(2), .width(32), .enable("false")) multiplexer_2 (
    .in0(register_1_q), .in1(register_2_q), .in2(register_3_q), .in3(register_4_q), .out(B), .sel(B_addr));
endmodule

module RegisterFile16 (
  input  [31:0] in_1,
  input  in_2,
  input  [3:0] in_3,
  input  in_4,
  input  [3:0] in_5,
  input  [3:0] in_6,
  output [31:0] A,
  output [31:0] B
);

  wire demultiplexer_1_out0, demultiplexer_1_out1, demultiplexer_1_out2, demultiplexer_1_out3;
  wire [31:0] registerfile4_1_a, registerfile4_1_b, registerfile4_2_a, registerfile4_2_b, registerfile4_3_a,
       registerfile4_3_b, registerfile4_4_a, registerfile4_4_b;

  Demultiplexer #(.select(2), .enable("false")) demultiplexer_1 (
    .out0(demultiplexer_1_out0), .out1(demultiplexer_1_out1), .out2(demultiplexer_1_out2),
    .out3(demultiplexer_1_out3), .in(in_2), .sel(in_3[3:2]));
  RegisterFile4 registerfile4_1 (
    .w_data(in_1), .write_enable(demultiplexer_1_out0), .write_address(in_3[1:0]), .clock(in_4),
    .A_addr(in_5[1:0]), .B_addr(in_6[1:0]), .A(registerfile4_1_a), .B(registerfile4_1_b));
  RegisterFile4 registerfile4_2 (
    .w_data(in_1), .write_enable(demultiplexer_1_out1), .write_address(in_3[1:0]), .clock(in_4),
    .A_addr(in_5[1:0]), .B_addr(in_6[1:0]), .A(registerfile4_2_a), .B(registerfile4_2_b));
  RegisterFile4 registerfile4_3 (
    .w_data(in_1), .write_enable(demultiplexer_1_out2), .write_address(in_3[1:0]), .clock(in_4),
    .A_addr(in_5[1:0]), .B_addr(in_6[1:0]), .A(registerfile4_3_a), .B(registerfile4_3_b));
  RegisterFile4 registerfile4_4 (
    .w_data(in_1), .write_enable(demultiplexer_1_out3), .write_address(in_3[1:0]), .clock(in_4),
    .A_addr(in_5[1:0]), .B_addr(in_6[1:0]), .A(registerfile4_4_a), .B(registerfile4_4_b));
  Multiplexer #(.select(2), .width(32), .enable("false")) multiplexer_1 (
    .in0(registerfile4_1_a), .in1(registerfile4_2_a), .in2(registerfile4_3_a), .in3(registerfile4_4_a),
    .out(A), .sel(in_5[3:2]));
  Multiplexer #(.select(2), .width(32), .enable("false")) multiplexer_2 (
    .in0(registerfile4_1_b), .in1(registerfile4_2_b), .in2(registerfile4_3_b), .in3(registerfile4_4_b),
    .out(B), .sel(in_6[3:2]));
endmodule

// RegFile
module RegisterFile32 (
  input  [31:0] w_data,
  input  write_enable,
  input  [4:0] write_addr,
  input  CLK,
  input  [4:0] A_addr,
  input  [4:0] B_addr,
  output [31:0] A,
  output [31:0] B
);

  wire demultiplexer_1_out0, demultiplexer_1_out1;
  wire [31:0] registerfile16_1_a, registerfile16_1_b, registerfile16_2_a, registerfile16_2_b;

  Demultiplexer #(.enable("false")) demultiplexer_1 (
    .out0(demultiplexer_1_out0), .out1(demultiplexer_1_out1), .in(write_enable), .sel(write_addr[4]));
  RegisterFile16 registerfile16_1 (
    .in_1(w_data), .in_2(demultiplexer_1_out0), .in_3(write_addr[3:0]), .in_4(CLK), .in_5(A_addr[3:0]),
    .in_6(B_addr[3:0]), .A(registerfile16_1_a), .B(registerfile16_1_b));
  RegisterFile16 registerfile16_2 (
    .in_1(w_data), .in_2(demultiplexer_1_out1), .in_3(write_addr[3:0]), .in_4(CLK), .in_5(A_addr[3:0]),
    .in_6(B_addr[3:0]), .A(registerfile16_2_a), .B(registerfile16_2_b));
  Multiplexer #(.width(32), .enable("false")) multiplexer_1 (
    .in0(registerfile16_1_a), .in1(registerfile16_2_a), .out(A), .sel(A_addr[4]));
  Multiplexer #(.width(32), .enable("false")) multiplexer_2 (
    .in0(registerfile16_1_b), .in1(registerfile16_2_b), .out(B), .sel(B_addr[4]));
endmodule

module Jtypever (
  input  [31:0] instr,
  input  CLK,
  input  [31:0] C,
  output [31:0] A,
  output [31:0] B,
  output immtype,
  output [31:0] dataforSW,
  output [31:0] out_8
);

  wire [4:0] multiplexer_1_out;
  wire [31:0] bit_extender_2_out;

  Multiplexer #(.width(5), .enable("false")) multiplexer_1 (
    .in0(instr[15:11]), .in1(instr[20:16]), .out(multiplexer_1_out), .sel(immtype));
  assign out_8 = {{6{instr[25]}}, instr[25:0]};  // Bit_Extender bit_extender_1
  RegisterFile32 registerfile32_1 (
    .w_data(C), .write_enable(1'b1), .write_addr(multiplexer_1_out), .CLK(CLK), .A_addr(instr[25:21]),
    .B_addr(instr[20:16]), .A(A), .B(dataforSW));
  Multiplexer #(.width(32), .enable("false")) multiplexer_2 (
    .in0(dataforSW), .in1(bit_extender_2_out), .out(B), .sel(immtype));
  assign bit_extender_2_out = {{16{instr[15]}}, instr[15:0]};  // Bit_Extender bit_extender_2
  or or_1 (immtype, instr[26], instr[27], instr[28], instr[29], instr[30], instr[31]);

  // Notes on the sheet:
  //   R-type
  //   func
  //   shmat
  //   rd
  //   rt
  //   rs
  //   op
  //   I-type
  //   imm
  //   rt
  //   rs
  //   op
  //   addr
  //   op
endmodule

module ALU (
  input  [31:0] A,
  input  [31:0] B,
  input  [2:0] Sel,
  output [31:0] C,
  output zero,
  output Not_zero
);

  wire [31:0] adder_1_out, subtractor_1_out;

  Adder #(.width(32)) adder_1 (.a(A), .b(B), .out(adder_1_out));  // open: cin, cout
  Subtractor #(.width(32)) subtractor_1 (.a(A), .b(B), .out(subtractor_1_out));  // open: bin, bout
  Comparator #(.width(32)) comparator_1 (.a(A), .b(B), .gt(Not_zero), .eq(zero));  // open: lt
  Multiplexer #(.width(32), .enable("false")) multiplexer_1 (
    .in0(adder_1_out), .in1(subtractor_1_out), .out(C), .sel(Sel[0]));
endmodule

module arthmetic_calc (
  input  [31:0] in_1,
  input  [31:0] in_2,
  input  [1:0] in_3,
  output [31:0] out_4
);

  wire [31:0] adder_1_out, divider_1_out, shifter_1_out, subtractor_1_out;

  Adder #(.width(32)) adder_1 (.a(in_1), .b(in_2), .out(adder_1_out));  // open: cin, cout
  Subtractor #(.width(32)) subtractor_1 (.a(in_1), .b(in_2), .out(subtractor_1_out));  // open: bin, bout
  Shifter #(.width(32)) shifter_1 (.in(in_1), .\dist (in_2[4:0]), .out(shifter_1_out));
  Divider #(.width(32)) divider_1 (.a(in_1), .b(in_2), .out(divider_1_out));  // open: upper, rem
  Multiplexer #(.select(2), .width(32), .enable("false")) multiplexer_1 (
    .in0(adder_1_out), .in1(subtractor_1_out), .in2(shifter_1_out), .in3(divider_1_out), .out(out_4),
    .sel(in_3));
endmodule

module halfadder (
  input  in_1,
  input  in_2,
  output out_3,
  output out_4
);

  and and_1 (out_3, in_1, in_2);
  xor xor_1 (out_4, in_1, in_2);

  // Notes on the sheet:
  //   sum = x xor y
  //   <Half Adder>
endmodule

module logical_calc (
  input  [31:0] in_1,
  input  [31:0] in_2,
  input  [1:0] in_3,
  output [31:0] out_4
);

  wire [31:0] and_1_out, nor_1_out, or_1_out, xor_1_out;

  assign and_1_out = in_1 & in_2;  // AND_Gate and_1, 32 bits wide
  assign or_1_out = in_1 | in_2;  // OR_Gate or_1, 32 bits wide
  assign nor_1_out = ~(in_1 | in_2);  // NOR_Gate nor_1, 32 bits wide
  assign xor_1_out = in_1 ^ in_2;  // XOR_Gate xor_1, 32 bits wide
  Multiplexer #(.select(2), .width(32), .enable("false")) multiplexer_1 (
    .in0(and_1_out), .in1(or_1_out), .in2(nor_1_out), .in3(xor_1_out), .out(out_4), .sel(in_3));
endmodule

module SRlatch (
  input  R,
  input  S,
  output out_3
);

  wire nor_2_out;

  nor nor_1 (out_3, R, nor_2_out);
  nor nor_2 (nor_2_out, out_3, S);

  // Notes on the sheet:
  //   SR Latch
endmodule

module Dlatch (
  input  C,
  input  D,
  output out_3
);

  wire and_1_out, and_2_out, not_1_out;

  not not_1 (not_1_out, D);
  and and_1 (and_1_out, C, not_1_out);
  SRlatch srlatch_1 (.R(and_1_out), .S(and_2_out), .out_3(out_3));
  and and_2 (and_2_out, C, D);

  // Notes on the sheet:
  //   When C=0, no output changes
  //   When C=1, output changes as input D changes.
  //   D Latch
endmodule

module D_FF (
  input  C,
  input  D,
  output out_3
);

  wire dlatch_1_out_3, not_1_out;

  not not_1 (not_1_out, C);
  Dlatch dlatch_1 (.C(not_1_out), .D(D), .out_3(dlatch_1_out_3));
  Dlatch dlatch_2 (.C(C), .D(dlatch_1_out_3), .out_3(out_3));

  // Notes on the sheet:
  //   Master-Slave D-FF
endmodule

module Jtype_ID (
  input  [31:0] instr,
  input  CLK,
  input  [31:0] C_value_in,
  output [31:0] A,
  output [31:0] B,
  output [31:0] dataforSW,
  output [31:0] imm,
  output [2:0] ALUoperation,
  output MemRead,
  output MemWrite,
  output MemtoReg,
  output PCSrc,
  output [31:0] out_13
);

  wire [2:0] rom_2_data;
  wire [4:0] multiplexer_1_out, rom_1_data;

  ROM #(.addrWidth(6), .dataWidth(9)) rom_1 (
    .addr(instr[31:26]), .data({PCSrc, MemtoReg, MemWrite, MemRead, rom_1_data}));
  assign out_13 = {{6{instr[25]}}, instr[25:0]};  // Bit_Extender bit_extender_1
  Multiplexer #(.width(5), .enable("false")) multiplexer_1 (
    .in0(instr[15:11]), .in1(instr[20:16]), .out(multiplexer_1_out), .sel(rom_1_data[4]));
  RegisterFile32 registerfile32_1 (
    .w_data(C_value_in), .write_enable(rom_1_data[3]), .write_addr(multiplexer_1_out), .CLK(CLK),
    .A_addr(instr[25:21]), .B_addr(instr[20:16]), .A(A), .B(dataforSW));
  Multiplexer #(.width(32), .enable("false")) multiplexer_2 (.in0(dataforSW), .in1(imm), .out(B), .sel(rom_1_data[4]));
  assign imm = {{16{instr[15]}}, instr[15:0]};  // Bit_Extender bit_extender_2
  ROM #(.addrWidth(6), .dataWidth(3)) rom_2 (.addr(instr[5:0]), .data(rom_2_data));
  Multiplexer #(.width(3), .enable("false")) multiplexer_3 (
    .in0(rom_2_data), .in1(rom_1_data[2:0]), .out(ALUoperation), .sel(rom_1_data[4]));

  // Notes on the sheet:
  //   R-format:0 0 0 0 0 1 000
  //   lw: 0 /1 0 1 1 /1 000
  //   sw: 0/ 0 1 0 1/ 0 000
  //   beq: 1/ 0 0 0 0/ 0 000
  //   addi: 0/ 0 0 0 1/ 1 000
  //   contents of rom_1 (hex, n*v repeats v):
  //   8 0 0 0 100 0 0 0 18 26*0 b8 7*0 50
  //   op lw: 10/0011
  //   op sw: 10/1011
  //   op beq: 00/0100
  //   op addi: 00/1000
  //   addr
  //   op
  //   R-type
  //   func
  //   shmat
  //   rd
  //   rt
  //   rs
  //   op
  //   I-type
  //   imm
  //   rt
  //   rs
  //   op
  //   RegWrite
  //   ALUsrc
  //   branch/sw not update reg
  //   end
  //   start
  //   selbit=0, R-format
  //   R-type's function part->because we dont know opcode in R-format
  //   addition:000
endmodule

module JtypeMIPSProcessor (
  input  Reset,
  input  CLK
);

  wire if_1_p3, if_1_p4, jtype_id_1_memread, jtype_id_1_memtoreg, jtype_id_1_memwrite;
  wire [2:0] jtype_id_1_aluoperation;
  wire [31:0] alu_1_c, if_1_p5, if_1_p6, jtype_id_1_a, jtype_id_1_b, jtype_id_1_dataforsw, multiplexer_1_out,
       ram_1_dout;

  // IF if_1: pin names not known; wires that end beside it: CLK, Reset, if_1_p3, if_1_p4, if_1_p5, if_1_p6
  Multiplexer #(.width(32), .enable("false")) multiplexer_1 (
    .in0(alu_1_c), .in1(ram_1_dout), .out(multiplexer_1_out), .sel(jtype_id_1_memtoreg));
  Jtype_ID jtype_id_1 (
    .instr(if_1_p6), .CLK(CLK), .C_value_in(multiplexer_1_out), .A(jtype_id_1_a), .B(jtype_id_1_b),
    .dataforSW(jtype_id_1_dataforsw), .imm(if_1_p5), .ALUoperation(jtype_id_1_aluoperation),
    .MemRead(jtype_id_1_memread), .MemWrite(jtype_id_1_memwrite), .MemtoReg(jtype_id_1_memtoreg),
    .PCSrc(if_1_p3));  // open: out_13
  ALU alu_1 (
    .A(jtype_id_1_a), .B(jtype_id_1_b), .Sel(jtype_id_1_aluoperation), .C(alu_1_c), .zero(if_1_p4));  // open: Not_zero
  RAM #(.dataWidth(32), .databus("bibus")) ram_1 (
    .addr(alu_1_c[9:2]), .we(jtype_id_1_memwrite), .oe(jtype_id_1_memread), .clk(CLK),
    .din(jtype_id_1_dataforsw), .dout(ram_1_dout));

  // Notes on the sheet:
  //   C is input
endmodule
